// Digital circuit control-unit.dig as structural Verilog
module control_unit (
  input  [6:0] opcode,
  input  [2:0] funct3,
  input  [6:0] funct7,
  output RegWrite,
  output ALUSrc,
  output [1:0] ImmSrc,
  output [3:0] ALUOp
);

  wire and_1_out, and_2_out, and_3_out, and_4_out, and_5_out, and_6_out, and_7_out, and_8_out,
       comparator_1_eq, comparator_2_eq, comparator_3_eq, comparator_4_eq, comparator_5_eq, comparator_6_eq,
       comparator_7_eq, comparator_8_eq;
  wire [2:0] priorityencoder_1_num;

  Comparator #(.Bits(7)) comparator_1 (.a(opcode), .b(7'b0110011), .eq(comparator_1_eq));  // open: gt, lt
  Comparator #(.Bits(7)) comparator_2 (.a(opcode), .b(7'b0010011), .eq(comparator_2_eq));  // open: gt, lt
  Comparator #(.Bits(3)) comparator_3 (.a(funct3), .b(3'b000), .eq(comparator_3_eq));  // open: gt, lt
  Comparator #(.Bits(3)) comparator_4 (.a(funct3), .b(3'b010), .eq(comparator_4_eq));  // open: gt, lt
  Comparator #(.Bits(3)) comparator_5 (.a(funct3), .b(3'b110), .eq(comparator_5_eq));  // open: gt, lt
  Comparator #(.Bits(3)) comparator_6 (.a(funct3), .b(3'b111), .eq(comparator_6_eq));  // open: gt, lt
  Comparator #(.Bits(7)) comparator_7 (.a(funct7), .b({7{1'b0}}), .eq(comparator_7_eq));  // open: gt, lt
  Comparator #(.Bits(7)) comparator_8 (.a(funct7), .b(7'b0100000), .eq(comparator_8_eq));  // open: gt, lt
  and and_1 (and_1_out, comparator_1_eq, comparator_3_eq, comparator_7_eq);
  and and_2 (and_2_out, comparator_1_eq, comparator_3_eq, comparator_8_eq);
  and and_3 (and_3_out, comparator_1_eq, comparator_6_eq, comparator_7_eq);
  and and_4 (and_4_out, comparator_1_eq, comparator_5_eq, comparator_7_eq);
  and and_5 (and_5_out, comparator_1_eq, comparator_4_eq, comparator_7_eq);
  and and_6 (and_6_out, comparator_2_eq, comparator_3_eq);
  and and_7 (and_7_out, comparator_2_eq, comparator_4_eq);
  and and_8 (and_8_out, comparator_2_eq, comparator_6_eq);
  PriorityEncoder #(.Selector_Bits(3)) priorityencoder_1 (
    .in0(and_1_out), .in1(and_2_out), .in2(and_3_out), .in3(and_4_out), .in4(and_5_out), .in5(and_6_out),
    .in6(and_7_out), .in7(and_8_out), .num(priorityencoder_1_num));  // open: any
  ROM #(.AddrBits(3), .Bits(8)) rom_1 (.A(priorityencoder_1_num), .sel(1'b1), .D({RegWrite, ALUSrc, ImmSrc, ALUOp}));

  // Notes on the sheet:
  //   contents of rom_1 (hex, n*v repeats v):
  //   82,86,80,81,87,c2,c7,c0
endmodule

/* Test case ControlTest:
# Columns: Inputs followed by Expected Outputs
opcode funct3 funct7    RegWrite ALUSrc ImmSrc ALUOp

# 0: ADD (R-Type, Add) -> Expect ROM Addr 0
51     0      0         1        0      0      2

# 1: SUB (R-Type, Sub) -> Expect ROM Addr 1
51     0      32        1        0      0      6

# 2: AND (R-Type, And) -> Expect ROM Addr 2
51     7      0         1        0      0      0

# 3: OR  (R-Type, Or)  -> Expect ROM Addr 3
51     6      0         1        0      0      1

# 4: SLT (R-Type, Slt) -> Expect ROM Addr 4
51     2      0         1        0      0      7

# 5: ADDI (I-Type, Add) -> Expect ROM Addr 5
19     0      0         1        1      0      2

# 6: SLTI (I-Type, Slt) -> Expect ROM Addr 6
19     2      0         1        1      0      7

# 7: ANDI (I-Type, And) -> Expect ROM Addr 7
19     7      0         1        1      0      0
        
*/
