// Digital circuit register-file.dig as structural Verilog
module register_file (
  input  [4:0] ReadReg1,
  input  [4:0] ReadReg2,
  input  [4:0] WriteReg,
  input  [31:0] WriteData,
  input  RegWrite,
  input  Clock,
  output [31:0] ReadData1,
  output [31:0] ReadData2
);

  wire and_1_out, and_2_out, and_3_out, and_4_out, and_5_out, and_6_out, and_7_out, and_8_out, and_9_out,
       and_10_out, and_11_out, and_12_out, and_13_out, and_14_out, and_15_out, and_16_out, and_17_out,
       and_18_out, and_19_out, and_20_out, and_21_out, and_22_out, and_23_out, and_24_out, and_25_out,
       and_26_out, and_27_out, and_28_out, and_29_out, and_30_out, and_31_out, decoder_1_out_1,
       decoder_1_out_2, decoder_1_out_3, decoder_1_out_4, decoder_1_out_5, decoder_1_out_6, decoder_1_out_7,
       decoder_1_out_8, decoder_1_out_9, decoder_1_out_10, decoder_1_out_11, decoder_1_out_12,
       decoder_1_out_13, decoder_1_out_14, decoder_1_out_15, decoder_1_out_16, decoder_1_out_17,
       decoder_1_out_18, decoder_1_out_19, decoder_1_out_20, decoder_1_out_21, decoder_1_out_22,
       decoder_1_out_23, decoder_1_out_24, decoder_1_out_25, decoder_1_out_26, decoder_1_out_27,
       decoder_1_out_28, decoder_1_out_29, decoder_1_out_30, decoder_1_out_31;
  wire [31:0] R1_Out, R2_Out, R3_Out, R4_Out, R5_Out, R6_Out, R7_Out, R8_Out, R9_Out, R10_Out, R11_Out,
       R12_Out, R13_Out, R14_Out, R15_Out, R16_Out, R17_Out, R18_Out, R19_Out, R20_Out, R21_Out, R22_Out,
       R23_Out, R24_Out, R25_Out, R26_Out, R27_Out, R28_Out, R29_Out, R30_Out, R31_Out;

  Decoder #(.Selector_Bits(5)) decoder_1 (
    .sel(WriteReg), .out_1(decoder_1_out_1), .out_2(decoder_1_out_2), .out_3(decoder_1_out_3),
    .out_4(decoder_1_out_4), .out_5(decoder_1_out_5), .out_6(decoder_1_out_6), .out_7(decoder_1_out_7),
    .out_8(decoder_1_out_8), .out_9(decoder_1_out_9), .out_10(decoder_1_out_10), .out_11(decoder_1_out_11),
    .out_12(decoder_1_out_12), .out_13(decoder_1_out_13), .out_14(decoder_1_out_14),
    .out_15(decoder_1_out_15), .out_16(decoder_1_out_16), .out_17(decoder_1_out_17),
    .out_18(decoder_1_out_18), .out_19(decoder_1_out_19), .out_20(decoder_1_out_20),
    .out_21(decoder_1_out_21), .out_22(decoder_1_out_22), .out_23(decoder_1_out_23),
    .out_24(decoder_1_out_24), .out_25(decoder_1_out_25), .out_26(decoder_1_out_26),
    .out_27(decoder_1_out_27), .out_28(decoder_1_out_28), .out_29(decoder_1_out_29),
    .out_30(decoder_1_out_30), .out_31(decoder_1_out_31));  // open: out_0
  and and_1 (and_1_out, decoder_1_out_1, RegWrite);
  and and_2 (and_2_out, decoder_1_out_2, RegWrite);
  and and_3 (and_3_out, decoder_1_out_3, RegWrite);
  and and_4 (and_4_out, decoder_1_out_4, RegWrite);
  and and_5 (and_5_out, decoder_1_out_5, RegWrite);
  and and_6 (and_6_out, decoder_1_out_6, RegWrite);
  and and_7 (and_7_out, decoder_1_out_7, RegWrite);
  and and_8 (and_8_out, decoder_1_out_8, RegWrite);
  and and_9 (and_9_out, decoder_1_out_9, RegWrite);
  and and_10 (and_10_out, decoder_1_out_10, RegWrite);
  and and_11 (and_11_out, decoder_1_out_11, RegWrite);
  and and_12 (and_12_out, decoder_1_out_12, RegWrite);
  and and_13 (and_13_out, decoder_1_out_13, RegWrite);
  and and_14 (and_14_out, decoder_1_out_14, RegWrite);
  and and_15 (and_15_out, decoder_1_out_15, RegWrite);
  and and_16 (and_16_out, decoder_1_out_16, RegWrite);
  and and_17 (and_17_out, decoder_1_out_17, RegWrite);
  and and_18 (and_18_out, decoder_1_out_18, RegWrite);
  and and_19 (and_19_out, decoder_1_out_19, RegWrite);
  and and_20 (and_20_out, decoder_1_out_20, RegWrite);
  and and_21 (and_21_out, decoder_1_out_21, RegWrite);
  and and_22 (and_22_out, decoder_1_out_22, RegWrite);
  and and_23 (and_23_out, decoder_1_out_23, RegWrite);
  and and_24 (and_24_out, decoder_1_out_24, RegWrite);
  and and_25 (and_25_out, decoder_1_out_25, RegWrite);
  and and_26 (and_26_out, decoder_1_out_26, RegWrite);
  and and_27 (and_27_out, decoder_1_out_27, RegWrite);
  and and_28 (and_28_out, decoder_1_out_28, RegWrite);
  and and_29 (and_29_out, decoder_1_out_29, RegWrite);
  and and_30 (and_30_out, decoder_1_out_30, RegWrite);
  and and_31 (and_31_out, decoder_1_out_31, RegWrite);
  Register #(.Bits(32)) _1 (.D(WriteData), .C(Clock), .en(and_1_out), .Q(R1_Out));
  Register #(.Bits(32)) _2 (.D(WriteData), .C(Clock), .en(and_2_out), .Q(R2_Out));
  Register #(.Bits(32)) _3 (.D(WriteData), .C(Clock), .en(and_3_out), .Q(R3_Out));
  Register #(.Bits(32)) _4 (.D(WriteData), .C(Clock), .en(and_4_out), .Q(R4_Out));
  Register #(.Bits(32)) _5 (.D(WriteData), .C(Clock), .en(and_5_out), .Q(R5_Out));
  Register #(.Bits(32)) _6 (.D(WriteData), .C(Clock), .en(and_6_out), .Q(R6_Out));
  Register #(.Bits(32)) _7 (.D(WriteData), .C(Clock), .en(and_7_out), .Q(R7_Out));
  Register #(.Bits(32)) _8 (.D(WriteData), .C(Clock), .en(and_8_out), .Q(R8_Out));
  Register #(.Bits(32)) _9 (.D(WriteData), .C(Clock), .en(and_9_out), .Q(R9_Out));
  Register #(.Bits(32)) _10 (.D(WriteData), .C(Clock), .en(and_10_out), .Q(R10_Out));
  Register #(.Bits(32)) _11 (.D(WriteData), .C(Clock), .en(and_11_out), .Q(R11_Out));
  Register #(.Bits(32)) _12 (.D(WriteData), .C(Clock), .en(and_12_out), .Q(R12_Out));
  Register #(.Bits(32)) _13 (.D(WriteData), .C(Clock), .en(and_13_out), .Q(R13_Out));
  Register #(.Bits(32)) _14 (.D(WriteData), .C(Clock), .en(and_14_out), .Q(R14_Out));
  Register #(.Bits(32)) _15 (.D(WriteData), .C(Clock), .en(and_15_out), .Q(R15_Out));
  Register #(.Bits(32)) _16 (.D(WriteData), .C(Clock), .en(and_16_out), .Q(R16_Out));
  Register #(.Bits(32)) _17 (.D(WriteData), .C(Clock), .en(and_17_out), .Q(R17_Out));
  Register #(.Bits(32)) _18 (.D(WriteData), .C(Clock), .en(and_18_out), .Q(R18_Out));
  Register #(.Bits(32)) _19 (.D(WriteData), .C(Clock), .en(and_19_out), .Q(R19_Out));
  Register #(.Bits(32)) _20 (.D(WriteData), .C(Clock), .en(and_20_out), .Q(R20_Out));
  Register #(.Bits(32)) _21 (.D(WriteData), .C(Clock), .en(and_21_out), .Q(R21_Out));
  Register #(.Bits(32)) _22 (.D(WriteData), .C(Clock), .en(and_22_out), .Q(R22_Out));
  Register #(.Bits(32)) _23 (.D(WriteData), .C(Clock), .en(and_23_out), .Q(R23_Out));
  Register #(.Bits(32)) _24 (.D(WriteData), .C(Clock), .en(and_24_out), .Q(R24_Out));
  Register #(.Bits(32)) _25 (.D(WriteData), .C(Clock), .en(and_25_out), .Q(R25_Out));
  Register #(.Bits(32)) _26 (.D(WriteData), .C(Clock), .en(and_26_out), .Q(R26_Out));
  Register #(.Bits(32)) _27 (.D(WriteData), .C(Clock), .en(and_27_out), .Q(R27_Out));
  Register #(.Bits(32)) _28 (.D(WriteData), .C(Clock), .en(and_28_out), .Q(R28_Out));
  Register #(.Bits(32)) _29 (.D(WriteData), .C(Clock), .en(and_29_out), .Q(R29_Out));
  Register #(.Bits(32)) _30 (.D(WriteData), .C(Clock), .en(and_30_out), .Q(R30_Out));
  Register #(.Bits(32)) _31 (.D(WriteData), .C(Clock), .en(and_31_out), .Q(R31_Out));
  Multiplexer #(.Selector_Bits(5), .Bits(32)) multiplexer_1 (
    .sel(ReadReg1), .in_0({32{1'b0}}), .in_1(R1_Out), .in_2(R2_Out), .in_3(R3_Out), .in_4(R4_Out),
    .in_5(R5_Out), .in_6(R6_Out), .in_7(R7_Out), .in_8(R8_Out), .in_9(R9_Out), .in_10(R10_Out),
    .in_11(R11_Out), .in_12(R12_Out), .in_13(R13_Out), .in_14(R14_Out), .in_15(R15_Out), .in_16(R16_Out),
    .in_17(R17_Out), .in_18(R18_Out), .in_19(R19_Out), .in_20(R20_Out), .in_21(R21_Out), .in_22(R22_Out),
    .in_23(R23_Out), .in_24(R24_Out), .in_25(R25_Out), .in_26(R26_Out), .in_27(R27_Out), .in_28(R28_Out),
    .in_29(R29_Out), .in_30(R30_Out), .in_31(R31_Out), .out(ReadData1));
  Multiplexer #(.Selector_Bits(5), .Bits(32)) multiplexer_2 (
    .sel(ReadReg2), .in_0({32{1'b0}}), .in_1(R1_Out), .in_2(R2_Out), .in_3(R3_Out), .in_4(R4_Out),
    .in_5(R5_Out), .in_6(R6_Out), .in_7(R7_Out), .in_8(R8_Out), .in_9(R9_Out), .in_10(R10_Out),
    .in_11(R11_Out), .in_12(R12_Out), .in_13(R13_Out), .in_14(R14_Out), .in_15(R15_Out), .in_16(R16_Out),
    .in_17(R17_Out), .in_18(R18_Out), .in_19(R19_Out), .in_20(R20_Out), .in_21(R21_Out), .in_22(R22_Out),
    .in_23(R23_Out), .in_24(R24_Out), .in_25(R25_Out), .in_26(R26_Out), .in_27(R27_Out), .in_28(R28_Out),
    .in_29(R29_Out), .in_30(R30_Out), .in_31(R31_Out), .out(ReadData2));
endmodule

/* Test case Register File Test:
WriteReg WriteData RegWrite Clock ReadReg1 ReadReg2 ReadData1 ReadData2

# $1 = 25
1 25 1 C 1 0 25 0

# $2 = 30
2 30 1 C 0 2 0 30

# $(N+1) = (N+1)
loop(N, 30)
	(N+1) (N+1) 1 C (N+1) (N) (N+1) (N)
end loop

# $(N+1) = N-60
loop(N, 30)
	(N+1) (N-60) 1 C (N+1) (N+1) (N-60) (N-60)
end loop

# Try writing to $0. This should not write anything
0 25 1 C 0 0 0 0

# try writing when RegWrite = 0
# (the registers should still have their old values)
loop(N, 30)
	(N+1) (N+80) 0 C (N+1) (N+1) (N-60) (N-60)
end loop
*/
